# Fritzing sketch PROYECTO CREBI ESP32-S3 JCHR Sketch (saved by Fritzing 1.0.4)
circuit board: 6.59348cm x 3.02454cm

parts:
  DHT11_1 = DHT11 module
  DHT11_2 = DHT11 module
  A1 = FireBeetle2-ESP32-S3

nets:
  VCC: DHT11_1.VCC, DHT11_2.VCC, A1.pin_26
  GND: DHT11_1.GND, DHT11_2.GND, A1.pin_28
  N1: DHT11_1.DATA, A1.Pin_39
  N2: DHT11_2.DATA, A1.pin_5

custom parts:
  DHT11 module: DHT11 black pcb module
  FireBeetle2-ESP32-S3: FireBeetle 2 ESP32-S3 is a high-performance main-controller built around the ESP32-S3-WROOM-1-N16R8 module. ESP32-S3-WROOM-1-N16R8 comes with 16MB Flash and 8MB PSRAM for storing more data.
