# Fritzing sketch P2_JGA (saved by Fritzing 1.0.4)
circuit board: 11.8021cm x 8.44622cm

parts:
  A1 = FireBeetle2-ESP32-S3
  3-Axis_Accelerometer3 = 3-Axis Accelerometer Breakout - MMA8452Q
  HC-SR04_Sensor_3 = HC-SR04 Ultrasonic Distance Sensor
  M1 = MAX7219 8x8 single Led Matrix Module
  Mod1 = KY-004 Key Switch Module [package="Breakout board"]
  Mod5 = KY-004 Key Switch Module [package="Breakout board"]

nets:
  N1: A1.pin_8, HC-SR04_Sensor_3.ECHO
  N2: A1.pin_9, HC-SR04_Sensor_3.TRIG
  N3: A1.pin_10, Mod5.S
  VCC: A1.pin_14, HC-SR04_Sensor_3.VCC, Mod5.Vin
  GND: A1.pin_16, A1.pin_28, 3-Axis_Accelerometer3.GND, HC-SR04_Sensor_3.GND, M1.I-VCC, M1.O-VCC, Mod1.-, Mod5.-
  3.3V: A1.pin_26, 3-Axis_Accelerometer3.3.3V, M1.I-GND, M1.O-GND, Mod1.Vin
  N4: A1.pin_33, 3-Axis_Accelerometer3.SCL, M1.I-CS
  N5: A1.pin_34, 3-Axis_Accelerometer3.SDA, M1.I-DIN
  N6: A1.Pin_37, Mod1.S

custom parts:
  FireBeetle2-ESP32-S3: FireBeetle 2 ESP32-S3 is a high-performance main-controller built around the ESP32-S3-WROOM-1-N16R8 module. ESP32-S3-WROOM-1-N16R8 comes with 16MB Flash and 8MB PSRAM for storing more data.
  MAX7219 8x8 single Led Matrix Module: Description: MAX7219 8x8 LedMatrix single Red Module Dimensions: 32x32mm Documents:
  KY-004 Key Switch Module: Arduino Key Switch Module Keyes KY-004 is a push button that will output a high signal when pressed.
