# Fritzing sketch P2 PLB Sketch (saved by Fritzing 1.0.4)
circuit board: 11.9307cm x 5.98623cm
breadboards: 1

parts:
  A1 = FireBeetle2-ESP32-S3
  Mod1 = KY-019 5V Relay Module [package="Breakout board"]
  Mod2 = KY-005 Infrared Transmitter Module [package="Breakout board"]
  Mod3 = KY-022 Infrared Receiver Module [package="Breakout board"]
  U1 = Keyes Tilt Switch [package=THT]
  J1 = Basic Servo

nets:
  N1: A1.pin_5, Mod2.S
  N2: A1.pin_6, Mod3.S
  N3: A1.pin_7, U1.signal
  N4: A1.pin_8, Mod1.S
  N5: A1.pin_9, J1.pulse
  N6: A1.pin_18, A1.pin_28, Mod1.-, Mod2.-, Mod3.-, U1.ground, J1.gnd
  VIN: A1.pin_26, Mod1.+, Mod2.Vin, Mod3.Vin, U1.power, J1.vcc

custom parts:
  FireBeetle2-ESP32-S3: FireBeetle 2 ESP32-S3 is a high-performance main-controller built around the ESP32-S3-WROOM-1-N16R8 module. ESP32-S3-WROOM-1-N16R8 comes with 16MB Flash and 8MB PSRAM for storing more data.
  KY-019 5V Relay Module: KY-019 5V Relay module, used to control AC circuits. (Special thanks to vanepp for fixing the PCB holes and other errors)
  KY-005 Infrared Transmitter Module: Arduino IR Transmitter Module Keyes KY-005, emits infrared light at 38KHz.
  KY-022 Infrared Receiver Module: KY-022 IR receiver module, reacts to 38kHz infrared light.
  Keyes Tilt Switch: Keyes Tilt Switch Sensor Module for Arduino (Works with Official Arduino Boards). Working voltage: 3.3V~5V; digital switch output (0 & 1); High sensitivity.
